# Fritzing sketch room-control-unit-scheme (saved by Fritzing 0.9.3b)
breadboards: 2

parts:
  Part2 = RFID-RC522-v3
  Part3 = RFID-RC522-v3
  Part4 = RFID-RC522-v3
  Part5 = Arduino Mega 2560 (Rev3)

nets:
  N1: Part2.SDA, Part5.D35
  N2: Part2.SCK, Part3.SCK, Part4.SCK, Part5.D52
  N3: Part2.MOSI, Part3.MOSI, Part4.MOSI, Part5.D51
  N4: Part2.MISO, Part3.MISO, Part4.MISO, Part5.D50
  GND: Part2.GND, Part3.GND, Part4.GND, Part5.GND
  N5: Part2.RST, Part3.RST, Part4.RST, Part5.D49
  3.3V: Part2.3.3V, Part3.3.3V, Part4.3.3V, Part5.3V3
  N6: Part3.SDA, Part5.D33
  N7: Part4.SDA, Part5.D31

notes:
  Implantable Device Bin
  Operating Room entrance/exit
  Pre-operating Room entrance/exit

custom parts:
  RFID-RC522-v3: A simple China made RFID-RC522 Reader (6x4 cm); do check the pin labels, as this is a MFRC522 based clone.
